# Fritzing sketch sketch (saved by Fritzing 0.9.4)
breadboards: 1

parts:
  Part1 = Arduino Nano (Rev3.0)
  LED1 = LED - 5mm [color="Green (565nm)" package="5 mm [THT]"]
  LED2 = LED - 5mm [color="Red (633nm)" package="5 mm [THT]"]
  LED3 = LED - 5mm [color="Yellow (585nm)" package="5 mm [THT]"]
  R1 = Resistor [tolerance=±5% resistance=220 package=THT]
  R2 = Resistor [tolerance=±5% resistance=220 package=THT]
  R3 = Resistor [tolerance=±5% resistance=220 package=THT]
  BAT1 = Battery Holders [package=battery-aa]
  R4 = Resistor [tolerance=±5% resistance=100k package=THT]
  R5 = Resistor [tolerance=±5% resistance=1M package=THT]

nets:
  N1: Part1.GND, LED1.cathode, LED2.cathode, LED3.cathode, BAT1.+, R4.Pin_0
  N2: Part1.D2, R3.Pin_0
  N3: Part1.D3, R2.Pin_0
  N4: Part1.D4, R1.Pin_0
  N5: Part1.A0, R4.Pin_1, R5.Pin_1
  N6: LED1.anode, R3.Pin_1
  N7: LED2.anode, R1.Pin_1
  N8: LED3.anode, R2.Pin_1
  N9: BAT1.-, R5.Pin_0
